# Fritzing sketch hochzeitsuhr (saved by Fritzing 0.9.3b)

parts:
  U1 = NodeMCU V1.0
  Bauteil1 = Adafruit 1.54" Tri-Color eInk / ePaper Display with SRAM [part_number=3625]
  GY-NEO6MV3 = SUP500F [package=sup500f]

nets:
  N1: U1.D1, Bauteil1.DC
  N2: U1.D2, Bauteil1.DISPCS
  N3: U1.D3, Bauteil1.RESET
  3V3: U1.3V3, Bauteil1.3.3V, GY-NEO6MV3.VCC
  GND: U1.GND, Bauteil1.GND, GY-NEO6MV3.GND
  N4: U1.D5, Bauteil1.SCLK
  N5: U1.D6, GY-NEO6MV3.RX-I
  N6: U1.D7, Bauteil1.MOSI
  N7: U1.D8, GY-NEO6MV3.TX-O

notes:
  GND: Black
  VCC: Red
  RX: Yellow
  TX: Green

custom parts:
  NodeMCU V1.0: ESP8266 based NodeMCU
  Adafruit 1.54" Tri-Color eInk / ePaper Display with SRAM: This small 1.54" tri-color display has 152x152 black and red ink pixels and a white-ish background. Using our Arduino library, you can create a 'frame buffer' with what pixels you want to have activated and then write that out to the display. We tossed a small SRAM chip on the back. This chip shares the SPI port the eInk display uses, so you only need one extra pin. And, no more frame-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
